# Fritzing sketch Hệ thống trồng nấm (saved by Fritzing 0.9.9b)
breadboards: 1

parts:
  SHT30_-_HT76 = DHT11 Humitidy and Temperature Sensor
  Relay = KF-301 Relay [package=THT]
  Mạch_chuyển_đổi_áp_DC-DC_12V/5V/3_3V = 电源转换模块
  ESP8266_Mode = ESP8266 NodeMCU LoLin module
  Máy_bơm = smd LED [color="Red (633nm)" package="0603 [SMD]"]

nets:
  N1: SHT30_-_HT76.VDD, Relay.power, Mạch_chuyển_đổi_áp_DC-DC_12V/5V/3_3V.Pin_17, Mạch_chuyển_đổi_áp_DC-DC_12V/5V/3_3V.Pin_18
  N2: SHT30_-_HT76.DATA, ESP8266_Mode.D1
  N3: SHT30_-_HT76.NULL, ESP8266_Mode.D2
  GND: SHT30_-_HT76.GND, Relay.ground, Relay.NO, Mạch_chuyển_đổi_áp_DC-DC_12V/5V/3_3V.Pin_1, Mạch_chuyển_đổi_áp_DC-DC_12V/5V/3_3V.Pin_2, Mạch_chuyển_đổi_áp_DC-DC_12V/5V/3_3V.Pin_6, Mạch_chuyển_đổi_áp_DC-DC_12V/5V/3_3V.Pin_9, ESP8266_Mode.GND
  N4: Relay.signal, ESP8266_Mode.D6
  N5: Relay.C, Máy_bơm.cathode
  N6: Mạch_chuyển_đổi_áp_DC-DC_12V/5V/3_3V.Pin_10, Mạch_chuyển_đổi_áp_DC-DC_12V/5V/3_3V.Pin_12, Máy_bơm.anode
  N7: Mạch_chuyển_đổi_áp_DC-DC_12V/5V/3_3V.Pin_13, ESP8266_Mode.3V3

custom parts:
  DHT11 Humitidy and Temperature Sensor: DHT11 Humidity and Temperature Sensor
  KF-301 Relay: KF-301
  电源转换模块: DC-DC 12V To 3.3V 5V Buck Step down Power Supply Module For Arduino
  ESP8266 NodeMCU LoLin module: ESP8266 based NodeMCU
